# Fritzing sketch ard (saved by Fritzing 0.9.3b)
perfboards: 1

parts:
  RFID_RC522_Reader = RFID-RC522-v2
  R1 = Resistor [tolerance=±5% resistance=220 package=THT]
  R2 = Resistor [tolerance=±5% resistance=220 package=THT]  # not connected
  R3 = Resistor [tolerance=±5% resistance=220 package=THT]
  LED1 = LED - 5mm [color="Red (633nm)" package="5 mm [THT]"]  # not connected
  LED2 = LED - 5mm [color="Red (633nm)" package="5 mm [THT]"]  # not connected
  LED3 = LED - 5mm [color="Red (633nm)" package="5 mm [THT]"]  # not connected
  Arduino_UNO_(Rev3) = Arduino Uno (Rev3)

nets:
  N1: RFID_RC522_Reader.SDA, Arduino_UNO_(Rev3).D10_PWM/SS
  N2: RFID_RC522_Reader.SCK, Arduino_UNO_(Rev3).D13/SCK
  N3: RFID_RC522_Reader.MOSI, Arduino_UNO_(Rev3).D11_PWM/MOSI
  N4: RFID_RC522_Reader.MISO, Arduino_UNO_(Rev3).D12/MISO
  GND: RFID_RC522_Reader.GND, Arduino_UNO_(Rev3).GND
  N5: RFID_RC522_Reader.RST, Arduino_UNO_(Rev3).D9_PWM
  3.3V: RFID_RC522_Reader.3.3V, Arduino_UNO_(Rev3).3V3
  N6: R1.Pin_1, R3.Pin_1

custom parts:
  RFID-RC522-v2: A simple China made RFID-RC522 Reader; do check the pin labels, as this is a MFRC522 based clone.

// code stored in the sketch: Untitled.ino
#include <MFRC522.h>
#include <SPI.h>

#define SS_PIN 10
#define RST_PIN 9

MFRC522 mfrc522(SS_PIN, RST_PIN);

const int LED_PIN_1 = 2;
const int LED_PIN_2 = 3;
const int LED_PIN_3 = 4;

int numCards = 0;
int **cardData = NULL;

void setup() {
  Serial.begin(9600);
  SPI.begin();
  mfrc522.PCD_Init();

  pinMode(LED_PIN_1, OUTPUT);
  pinMode(LED_PIN_2, OUTPUT);
  pinMode(LED_PIN_3, OUTPUT);
}

void loop() {
  if (mfrc522.PICC_IsNewCardPresent() && mfrc522.PICC_ReadCardSerial()) {
    int uidSize = mfrc522.uid.size;
    byte *uid = mfrc522.uid.uidByte;

    int cardIndex = -1;
    for (int i = 0; i < numCards; i++) {
      if (compareArrays(cardData[i], uid, uidSize)) {
        cardIndex = i;
        break;
      }
    }

    if (cardIndex == -1) {
      // Add new card to array
      int **newData = new int*[numCards + 1];
      for (int i = 0; i < numCards; i++) {
        newData[i] = cardData[i];
      }
      newData[numCards] = new int[uidSize];
      for (int i = 0; i < uidSize; i++) {
        newData[numCards][i] = uid[i];
      }
      numCards++;

      delete[] cardData;
      cardData = newData;

      // Turn on LED corresponding to number of cards
      switch (numCards) {
        case 1:
          digitalWrite(LED_PIN_1, HIGH);
          break;
        case 2:
          digitalWrite(LED_PIN_2, HIGH);
          break;
        case 3:
          digitalWrite(LED_PIN_3, HIGH);
          break;
      }
    } else {
      // Remove card from array
      removeElement(cardData, numCards, cardIndex);
      numCards--;

      // Turn off LED corresponding to number of cards
      switch (numCards) {
        case 0:
          digitalWrite(LED_PIN_1, LOW);
          digitalWrite(LED_PIN_2, LOW);
          digitalWrite(LED_PIN_3, LOW);
          break;
        case 1:
          digitalWrite(LED_PIN_2, LOW);
          digitalWrite(LED_PIN_3, LOW);
          break;
        case 2:
          digitalWrite(LED_PIN_3, LOW);
          break;
      }
    }

    mfrc522.PICC_HaltA();
    mfrc522.PCD_StopCrypto1();
  }
}

bool compareArrays(int* arr1, byte* arr2, int size) {
  for (int i = 0; i < size; i++) {
    if (arr1[i] != arr2[i]) {
      return false;
    }
  }
  return true;
}

void removeElement(int** arr, int size, int index) {
  for (int i = index; i < size - 1; i++) {
    arr[i] = arr[i + 1];
  }
}
